# Fritzing sketch CyGate4-Keypad (saved by Fritzing 0.9.3b)
circuit board: 8.46667cm x 5.64444cm
breadboards: 1

parts:
  J1 = screw terminal, 4 pins
  Arduino_Micro_Rev3 = Arduino Micro (Rev3)
  J2 = male pin header, 8 pins [form="♂ (male)"]
  J3 = male pin header, 5 pins [form="♂ (male)"]
  C1 = Ceramic Capacitor [capacitance=0.1mF package="100 mil [THT, multilayer]"]
  J4 = female pin header, 4 pins [form="♀ (female)"]
  J5 = female pin header, 4 pins [form="♀ (female)"]
  J6 = male pin header, 3 pins [form="♂ (male)"]
  J7 = male pin header, 3 pins [form="♂ (male)"]
  J8 = male pin header, 3 pins [form="♂ (male)"]

nets:
  N1: J1.pin1, Arduino_Micro_Rev3.GND, J3.pin1, C1.0, J5.pin4, J6.pin1, J7.pin1, J8.pin1
  N2: J1.pin2, Arduino_Micro_Rev3.5V, J3.pin2, J3.pin3, C1.1, J5.pin1, J6.pin3, J7.pin3, J8.pin3
  N3: J1.pin3, J5.pin3
  N4: J1.pin4, J5.pin2
  N5: Arduino_Micro_Rev3.D1/TX, J4.pin4
  N6: Arduino_Micro_Rev3.D0/RX, J4.pin1
  N7: Arduino_Micro_Rev3.D2/SDA, J4.pin2, J4.pin3
  N8: Arduino_Micro_Rev3.D4_PWM/A6, J2.pin8
  N9: Arduino_Micro_Rev3.D5_PWM, J2.pin7
  N10: Arduino_Micro_Rev3.D6_PWM/A7, J2.pin6
  N11: Arduino_Micro_Rev3.D7, J2.pin5
  N12: Arduino_Micro_Rev3.D8_PWM/A8, J2.pin4
  N13: Arduino_Micro_Rev3.D9_PWM/A9, J2.pin3
  N14: Arduino_Micro_Rev3.D10_PWM/A10, J2.pin2
  N15: Arduino_Micro_Rev3.D11_PWM, J2.pin1
  N16: Arduino_Micro_Rev3.D12_PWM/A11, J3.pin5
  N17: Arduino_Micro_Rev3.A2, J8.pin2
  N18: Arduino_Micro_Rev3.A1, J7.pin2
  N19: Arduino_Micro_Rev3.A0, J6.pin2
  N20: Arduino_Micro_Rev3.D13_PWM, J3.pin4

notes:
  KEYPAD
  1
  Gnd
  FAB 002001 ASSY 002001
  +5VDC
  A
  TX
  RX
  LCD
  CyGate4 - Keypad Rev 2.0
  Copyright (c) 2021 Cyrus Brunner
  www.cyrusbuilt.net
  CyGate4 - Keypad, Keypad entry and display module for CyGate4, 2.0
  GND
  To LCD
  To Keypad
  B
  DI
  DE
  RE
  RO
  VCC
  Address Select
  A0
  A1
  A2
  +
  -
  --------------------
  RS-485 Modbus Module
