# Fritzing sketch CyGate4-Keypad (saved by Fritzing 0.9.3b)
circuit board: 8.78777cm x 5.47896cm
breadboards: 1

parts:
  J1 = male pin header, 5 pins [form="♂ (male)"]
  Arduino_Micro_Rev3 = Arduino Micro (Rev3)
  J2 = male pin header, 8 pins [form="♂ (male)"]
  J3 = male pin header, 3 pins [form="♂ (male)"]
  J4 = male pin header, 3 pins [form="♂ (male)"]
  J5 = male pin header, 3 pins [form="♂ (male)"]
  R1 = Resistor [tolerance=±5% resistance=4.7k package=THT]
  R2 = Resistor [tolerance=±5% resistance=4.7k package=THT]
  J6 = screw terminal, 4 pins
  C1 = Ceramic Capacitor [capacitance=0.1mF package="100 mil [THT, multilayer]"]

nets:
  N1: J1.pin1, J1.pin5, Arduino_Micro_Rev3.GND, J3.pin1, J4.pin1, J5.pin1, J6.pin1, C1.0
  N2: J1.pin2, J1.pin3, Arduino_Micro_Rev3.5V, J3.pin3, J4.pin3, J5.pin3, R1.Pin_1, R2.Pin_1, J6.pin2, C1.1
  N3: J1.pin4, Arduino_Micro_Rev3.D13_PWM
  N4: Arduino_Micro_Rev3.D2/SDA, R1.Pin_0, J6.pin4
  N5: Arduino_Micro_Rev3.D3/SCL, R2.Pin_0, J6.pin3
  N6: Arduino_Micro_Rev3.D5_PWM, J2.pin8
  N7: Arduino_Micro_Rev3.D6_PWM/A7, J2.pin7
  N8: Arduino_Micro_Rev3.D7, J2.pin6
  N9: Arduino_Micro_Rev3.D8_PWM/A8, J2.pin5
  N10: Arduino_Micro_Rev3.D9_PWM/A9, J2.pin4
  N11: Arduino_Micro_Rev3.D10_PWM/A10, J2.pin3
  N12: Arduino_Micro_Rev3.D11_PWM, J2.pin2
  N13: Arduino_Micro_Rev3.D12_PWM/A11, J2.pin1
  N14: Arduino_Micro_Rev3.A2, J4.pin2
  N15: Arduino_Micro_Rev3.A1, J3.pin2
  N16: Arduino_Micro_Rev3.A0, J5.pin2

notes:
  Address Select
  To LCD
  -
  +
  A2
  A1
  A0
  GND
  +5VDC
  TX
  To Keypad
  SDA
  SCL
  <-- To CyGate4
  CyGate4 - Keypad, Keypad entry and display module for CyGate4, 1.0
  1
  LCD
  KEYPAD
  FAB 001001 ASSY 001001
  Gnd
  To CyGate4
  CyGate4 - Keypad Rev 1.0
  Copyright (c) 2021 Cyrus Brunner
  www.cyrusbuilt.net
